// Logisim project 2_input_Multiplexer.circ as structural Verilog: 1 circuit, main circuit main
module main (
);

  wire and_1_out, and_2_out, dipswitch_1_sw2, dipswitch_1_sw4, dipswitch_1_sw6, not_1_out, or_1_out;

  DipSwitch dipswitch_1 (
    .sw2(dipswitch_1_sw2), .sw4(dipswitch_1_sw4), .sw6(dipswitch_1_sw6));  // open: sw1, sw3, sw5, sw7, sw8
  not not_1 (not_1_out, dipswitch_1_sw6);
  and and_1 (and_1_out, dipswitch_1_sw2, dipswitch_1_sw6);
  and and_2 (and_2_out, dipswitch_1_sw4, not_1_out);
  or or_1 (or_1_out, and_1_out, and_2_out);
  LED led_1 (.in(or_1_out));
endmodule
