// Logisim project 3_input_LUT.circ as structural Verilog: 1 circuit, main circuit main
module main (
);

  wire button_1_out, d_ff_1_q, d_ff_2_q, d_ff_3_q, d_ff_4_q, d_ff_5_q, d_ff_6_q, d_ff_7_q, d_ff_8_q,
       dipswitch_1_sw1, dipswitch_1_sw2, dipswitch_1_sw3, dipswitch_1_sw4, dipswitch_1_sw5, dipswitch_1_sw6,
       dipswitch_1_sw7, dipswitch_1_sw8, multiplexer_1_out, undriven, undriven_2, undriven_3, undriven_4,
       undriven_5, undriven_6, undriven_7;
  wire [2:0] dipswitch_2_sw3;

  DipSwitch dipswitch_1 (
    .sw1(dipswitch_1_sw1), .sw2(dipswitch_1_sw2), .sw3(dipswitch_1_sw3), .sw4(dipswitch_1_sw4),
    .sw5(dipswitch_1_sw5), .sw6(dipswitch_1_sw6), .sw7(dipswitch_1_sw7), .sw8(dipswitch_1_sw8));
  D_Flip_Flop d_ff_1 (.D(dipswitch_1_sw1), .clk(button_1_out), .Q(d_ff_1_q), .reset(undriven));  // open: Qn, preset
  D_Flip_Flop d_ff_2 (
    .D(dipswitch_1_sw2), .clk(button_1_out), .Q(d_ff_2_q), .preset(undriven), .reset(undriven_2));  // open: Qn
  D_Flip_Flop d_ff_3 (
    .D(dipswitch_1_sw3), .clk(button_1_out), .Q(d_ff_3_q), .preset(undriven_2), .reset(undriven_3));  // open: Qn
  D_Flip_Flop d_ff_4 (
    .D(dipswitch_1_sw4), .clk(button_1_out), .Q(d_ff_4_q), .preset(undriven_3), .reset(undriven_4));  // open: Qn
  D_Flip_Flop d_ff_5 (
    .D(dipswitch_1_sw5), .clk(button_1_out), .Q(d_ff_5_q), .preset(undriven_4), .reset(undriven_5));  // open: Qn
  D_Flip_Flop d_ff_6 (
    .D(dipswitch_1_sw6), .clk(button_1_out), .Q(d_ff_6_q), .preset(undriven_5), .reset(undriven_6));  // open: Qn
  D_Flip_Flop d_ff_7 (
    .D(dipswitch_1_sw7), .clk(button_1_out), .Q(d_ff_7_q), .preset(undriven_6), .reset(undriven_7));  // open: Qn
  D_Flip_Flop d_ff_8 (.D(dipswitch_1_sw8), .clk(button_1_out), .Q(d_ff_8_q), .preset(undriven_7));  // open: Qn, reset
  Button button_1 (.out(button_1_out));
  DipSwitch dipswitch_2 (
    .sw1(dipswitch_2_sw3[2]), .sw2(dipswitch_2_sw3[1]), .sw3(dipswitch_2_sw3[0]));  // open: sw4, sw5, sw6, sw7, sw8
  Multiplexer #(.select(3), .enable("false")) multiplexer_1 (
    .in0(d_ff_1_q), .in1(d_ff_2_q), .in2(d_ff_3_q), .in3(d_ff_4_q), .in4(d_ff_5_q), .in5(d_ff_6_q),
    .in6(d_ff_7_q), .in7(d_ff_8_q), .out(multiplexer_1_out), .sel(dipswitch_2_sw3));
  LED led_1 (.in(multiplexer_1_out));
endmodule
