// Logisim project 4to1_mux.circ as structural Verilog: 1 circuit, main circuit main
module main (
);

  wire and_1_out, and_2_out, and_3_out, and_4_out, and_5_out, and_6_out, dipswitch_1_sw2, dipswitch_1_sw3,
       dipswitch_1_sw4, dipswitch_1_sw5, dipswitch_1_sw7, dipswitch_1_sw8, not_1_out, not_2_out, not_3_out,
       or_1_out, or_2_out, or_3_out;

  DipSwitch dipswitch_1 (
    .sw2(dipswitch_1_sw2), .sw3(dipswitch_1_sw3), .sw4(dipswitch_1_sw4), .sw5(dipswitch_1_sw5),
    .sw7(dipswitch_1_sw7), .sw8(dipswitch_1_sw8));  // open: sw1, sw6
  not not_1 (not_1_out, dipswitch_1_sw8);
  not not_2 (not_2_out, dipswitch_1_sw8);
  and and_1 (and_1_out, dipswitch_1_sw2, dipswitch_1_sw8);
  or or_1 (or_1_out, and_1_out, and_2_out);
  and and_2 (and_2_out, dipswitch_1_sw3, not_1_out);
  and and_3 (and_3_out, dipswitch_1_sw4, dipswitch_1_sw8);
  or or_2 (or_2_out, and_3_out, and_4_out);
  and and_4 (and_4_out, dipswitch_1_sw5, not_2_out);
  not not_3 (not_3_out, dipswitch_1_sw7);
  and and_5 (and_5_out, or_1_out, dipswitch_1_sw7);
  or or_3 (or_3_out, and_5_out, and_6_out);
  LED led_1 (.in(or_3_out));
  and and_6 (and_6_out, not_3_out, or_2_out);
endmodule
