// Logisim project BetterGatedLatch.circ as structural Verilog: 1 circuit, main circuit main
module main (
);

  wire and_1_out, buffer_1_out, dipswitch_1_sw7, dipswitch_1_sw8, nand_1_out, nand_2_out, nand_3_out,
       nand_5_out, not_1_out;

  DipSwitch dipswitch_1 (.sw7(dipswitch_1_sw7), .sw8(dipswitch_1_sw8));  // open: sw1, sw2, sw3, sw4, sw5, sw6
  not not_1 (not_1_out, dipswitch_1_sw8);
  and and_1 (and_1_out, dipswitch_1_sw8, buffer_1_out);
  buf buffer_1 (buffer_1_out, not_1_out);
  nand nand_1 (nand_1_out, dipswitch_1_sw7, and_1_out);
  nand nand_2 (nand_2_out, nand_1_out, and_1_out);
  nand nand_3 (nand_3_out, nand_1_out, nand_5_out);
  nand nand_4 (nand_3_out, nand_1_out, nand_5_out);
  nand nand_5 (nand_5_out, nand_3_out, nand_2_out);
  LED led_1 (.in(nand_3_out));
  LED led_2 (.in(nand_5_out));
endmodule
