// Logisim project ClockedDLatch.circ as structural Verilog: 1 circuit, main circuit main
module main (
);

  wire button_1_out, button_2_out, button_3_out, dipswitch_1_sw7, dipswitch_1_sw8, nand_1_out, nand_2_out,
       nand_3_out, nand_5_out;

  DipSwitch dipswitch_1 (.sw7(dipswitch_1_sw7), .sw8(dipswitch_1_sw8));  // open: sw1, sw2, sw3, sw4, sw5, sw6
  Button button_1 (.out(button_1_out));
  nand nand_1 (nand_1_out, dipswitch_1_sw7, button_1_out);
  nand nand_2 (nand_2_out, nand_1_out, button_1_out);
  Button button_2 (.out(button_2_out));
  Button button_3 (.out(button_3_out));
  nand nand_3 (nand_3_out, nand_1_out, button_2_out, nand_5_out);
  nand nand_4 (nand_3_out, nand_1_out, button_2_out, nand_5_out);
  nand nand_5 (nand_5_out, nand_3_out, button_3_out, nand_2_out);
  LED led_1 (.in(nand_3_out));
  LED led_2 (.in(nand_5_out));
endmodule
