// Logisim project Configurable_Logic_Block.circ as structural Verilog: 1 circuit, main circuit main
module main (
  output out_1
);

  wire clock_1_out, d_ff_1_q, dipswitch_2_sw1, undriven;
  wire [3:0] dipswitch_1_sw8;

  DipSwitch dipswitch_1 (
    .sw5(dipswitch_1_sw8[3]), .sw6(dipswitch_1_sw8[2]), .sw7(dipswitch_1_sw8[1]), .sw8(dipswitch_1_sw8[0]));  // open: sw1, sw2, sw3, sw4
  ROM #(.addrWidth(4), .dataWidth(1)) rom_1 (.addr(dipswitch_1_sw8));  // open: data
  D_Flip_Flop d_ff_1 (.D(undriven), .clk(clock_1_out), .Q(d_ff_1_q));  // open: Qn, preset, reset
  Clock clock_1 (.out(clock_1_out));
  DipSwitch #(.number(2)) dipswitch_2 (.sw1(dipswitch_2_sw1));  // open: sw2
  Multiplexer #(.enable("false")) multiplexer_1 (.in0(undriven), .in1(d_ff_1_q), .out(out_1), .sel(dipswitch_2_sw1));
endmodule
