// Logisim project Dtypeflipflop.circ as structural Verilog: 1 circuit, main circuit main
module main (
);

  wire clk_out, input_sw5, nand_1_out, nand_2_out, nand_3_out, nand_4_out, nand_5_out, nand_6_out,
       nand_7_out, nand_8_out, not_1_out;

  DipSwitch \input  (.sw5(input_sw5));  // open: sw1, sw2, sw3, sw4, sw6, sw7, sw8
  Button clk (.out(clk_out));
  nand nand_1 (nand_1_out, input_sw5, clk_out);
  nand nand_2 (nand_2_out, nand_1_out, clk_out);
  nand nand_3 (nand_3_out, nand_1_out, nand_4_out);
  nand nand_4 (nand_4_out, nand_3_out, nand_2_out);
  not not_1 (not_1_out, clk_out);
  nand nand_5 (nand_5_out, nand_3_out, not_1_out);
  nand nand_6 (nand_6_out, not_1_out, nand_4_out);
  nand nand_7 (nand_7_out, nand_5_out, nand_8_out);
  nand nand_8 (nand_8_out, nand_7_out, nand_6_out);
endmodule
