// Logisim project Latches.circ as structural Verilog: 1 circuit, main circuit main
module main (
);

  wire and_1_out, and_2_out, dipswitch_1_sw1, dipswitch_1_sw5, dipswitch_1_sw8, nand_1_out, nand_2_out,
       nand_3_out, nand_4_out, nor_1_out, nor_2_out;

  LED led_1 (.in(nor_1_out));
  nor nor_1 (nor_1_out, and_1_out, nor_2_out);
  and and_1 (and_1_out, dipswitch_1_sw1, dipswitch_1_sw5);
  DipSwitch dipswitch_1 (
    .sw1(dipswitch_1_sw1), .sw5(dipswitch_1_sw5), .sw8(dipswitch_1_sw8));  // open: sw2, sw3, sw4, sw6, sw7
  LED led_2 (.in(nor_2_out));
  nor nor_2 (nor_2_out, nor_1_out, and_2_out);
  and and_2 (and_2_out, dipswitch_1_sw5, dipswitch_1_sw8);
  nand nand_1 (nand_1_out, dipswitch_1_sw1, dipswitch_1_sw5);
  nand nand_2 (nand_2_out, dipswitch_1_sw5, dipswitch_1_sw8);
  nand nand_3 (nand_3_out, nand_1_out, nand_4_out);
  nand nand_4 (nand_4_out, nand_3_out, nand_2_out);
  LED led_3 (.in(nand_3_out));
  LED led_4 (.in(nand_4_out));
endmodule
